# Fritzing sketch Galvanico358 (saved by Fritzing 0.7.10b)
breadboards: 1

parts:
  J1 = screw terminal, 2 pins
  J2 = screw terminal, 2 pins
  U1 = LM 358 Dual Op-Amp [package="DIP8 [THT]"]
  R1 = Rotary Potentiometer (Small) [maximum_resistance=100kΩ]
  R10 = Rotary Potentiometer (Small) [maximum_resistance=100kΩ]
  G1 = female pin header, 1 pin [form="♀ (female)"]
  R3 = Resistor [tolerance=±5% resistance=220 package=THT]
  R4 = Resistor [tolerance=±5% resistance=220 package=THT]
  R5 = Resistor [tolerance=±5% resistance=220 package=THT]
  C1 = Electrolytic Capacitor [capacitance=1µF package="100 mil [THT, electrolytic]"]
  R6 = Resistor [tolerance=±5% resistance=220 package=THT]
  R7 = Resistor [tolerance=±5% resistance=220 package=THT]
  R8 = Resistor [tolerance=±5% resistance=220 package=THT]
  R9 = Resistor [tolerance=±5% resistance=220 package=THT]
  J3 = female pin header, 1 pin [form="♀ (female)"]

nets:
  N1: J1.pin1, J2.pin2, U1.connector3, R1.leg1, G1.pin1, C1.-, R9.Pin_1
  N2: J1.pin2, U1.connector7, R1.leg2, R7.Pin_1, R8.Pin_0
  N3: J2.pin1, R3.Pin_1, R7.Pin_0
  N4: U1.connector0, R4.Pin_0, R5.Pin_0
  N5: U1.connector1, R4.Pin_1, R6.Pin_0
  N6: U1.connector2, R3.Pin_0
  N7: R10.leg1, R8.Pin_1
  N8: R10.wiper, R6.Pin_1
  N9: R10.leg2, R9.Pin_0
  N10: R5.Pin_1, C1.+, J3.pin1

notes:
  Pulsu(m) Plantae
